# Fritzing sketch Platine (saved by Fritzing 1.0.3b)
circuit board: 7.2cm x 5.2cm
breadboards: 1

parts:
  ARD = Arduino Pro Mini (3.3V)
  MF_R = female pin header, 6 pins [form="♀ (female)"]
  MF_L = female pin header, 5 pins [form="♀ (female)"]
  CAM_L = female pin header, 7 pins [form="♀ (female)"]
  CAM_R = female pin header, 7 pins [form="♀ (female)"]
  RTC = female pin header, 6 pins [form="♀ (female)"]
  -_PIR = female pin header, 1 pin [form="♀ (female)"]
  -_PWR = female pin header, 1 pin [form="♀ (female)"]
  +_PWR = female pin header, 1 pin [form="♀ (female)"]
  A_PIR = female pin header, 1 pin [form="♀ (female)"]
  +_PIR = female pin header, 1 pin [form="♀ (female)"]

nets:
  N1: ARD.GND, MF_L.pin3, RTC.pin1, -_PIR.pin1, -_PWR.pin1
  N2: ARD.VCC, RTC.pin2, +_PIR.pin1
  N3: ARD.A0, MF_L.pin1
  N4: ARD.D10, CAM_R.pin7
  N5: ARD.D3, A_PIR.pin1
  N6: ARD.D2, RTC.pin5
  N7: MF_R.pin4, CAM_L.pin6
  N8: MF_R.pin6, CAM_L.pin7
  N9: MF_L.pin5, +_PWR.pin1
  N10: CAM_R.pin2, RTC.pin4
  N11: CAM_R.pin3, RTC.pin3
